# Fritzing sketch Primeiros passos (saved by Fritzing 0.8.7b)
breadboards: 1

parts:
  Componente1 = Arduino Uno (Rev3)
  LED1 = LED - 5mm [color="Red (633nm)" package="5 mm [THT]"]
  LED2 = LED_RING [package=led_ring]  # not connected
  R1 = Resistor [tolerance=±5% resistance=220 package=THT]
  Componente2 = Variable Capacitor [capacitance=100nF max_capacitance=10pF min_capacitance=2pF voltage=35V]  # not connected
  LED3 = LED - 5mm [color="Red (633nm)" package="5 mm [THT]"]  # not connected

nets:
  N1: Componente1.D13/SCK, LED1.anode
  N2: Componente1.GND, R1.Pin_0
  N3: LED1.cathode, R1.Pin_1

notes:
  On
  Off
  Print Temperature
  Switching Capacitor

// code stored in the sketch: Untitled 4.ino
programar arduino
